// Logisim project Apocalypse Computer.circ as structural Verilog: 9 circuits, main circuit main
module main (
  output [3:0] OP
);

  wire alpaca_1_out, clock_1_out, comparator_1_eq, comparator_2_eq, comparator_3_eq, comparator_4_eq,
       control_1_input_ram, control_1_load_byte, control_1_output_ram, control_1_pc___1,
       control_1_r_type_or_i_type, control_1_read_rf, control_1_save_byte, control_1_write_pc,
       control_1_write_rf, multiplexer_3_out, multiplexer_4_out, multiplexer_10_out, not_1_out, not_2_out;
  wire [1:0] i_type_split_1_rs, i_type_split_1_rt, multiplexer_1_out, multiplexer_2_out, r_type_split_1_rd,
       r_type_split_1_rs, r_type_split_1_rt;
  wire [2:0] control_1_alu_op;
  wire [3:0] multiplexer_6_out, multiplexer_6_out_2, r_type_split_1_opcode;
  wire [7:0] alu_1_result, i_type_split_1_immediate, multiplexer_5_out, multiplexer_7_out, multiplexer_8_out,
       multiplexer_9_out, pc_1_output, ram_1_data, registerfiles_1_register_1_out,
       registerfiles_1_register_2_out;
  wire [15:0] rom_1_data;

  r_type_split r_type_split_1 (
    .Input(rom_1_data), .RD(r_type_split_1_rd), .RT(r_type_split_1_rt), .RS(r_type_split_1_rs),
    .Opcode(r_type_split_1_opcode));
  i_type_split i_type_split_1 (
    .Input(rom_1_data), .Immediate(i_type_split_1_immediate), .RT(i_type_split_1_rt), .RS(i_type_split_1_rs),
    .Opcode(OP));
  Multiplexer #(.width(2)) multiplexer_1 (
    .in0(r_type_split_1_rd), .in1(r_type_split_1_rt), .out(multiplexer_1_out), .sel(control_1_save_byte));  // open: en
  Control control_1 (
    .OP_CODE(r_type_split_1_opcode), .Save_Byte(control_1_save_byte), .Read_RF(control_1_read_rf),
    .Write_RF(control_1_write_rf), .PC___1(control_1_pc___1), .Write_PC(control_1_write_pc),
    .Load_Byte(control_1_load_byte), .R_Type_or_I_Type(control_1_r_type_or_i_type),
    .Input_RAM(control_1_input_ram), .Output_RAM(control_1_output_ram), .ALU_OP(control_1_alu_op));
  Multiplexer #(.width(2)) multiplexer_2 (
    .in0(r_type_split_1_rt), .in1(r_type_split_1_rs), .out(multiplexer_2_out), .sel(control_1_save_byte));  // open: en
  Multiplexer multiplexer_3 (
    .in0(control_1_pc___1), .in1(1'b0), .out(multiplexer_3_out), .sel(alu_1_result[0]));  // open: en
  Comparator #(.width(4)) comparator_1 (.a(OP), .b(4'b0101), .eq(comparator_1_eq));  // open: gt, lt
  Multiplexer multiplexer_4 (
    .in0(multiplexer_3_out), .in1(control_1_pc___1), .out(multiplexer_4_out), .sel(not_1_out));  // open: en
  not not_1 (not_1_out, comparator_1_eq);
  registerFiles registerfiles_1 (
    .Write_Data(multiplexer_7_out), .toWrite(control_1_write_rf), .Read_Register_1(multiplexer_2_out),
    .toRead(control_1_read_rf), .Read_Register_2(multiplexer_1_out),
    .Register_1_OUT(registerfiles_1_register_1_out), .Register_2_OUT(registerfiles_1_register_2_out),
    .Write_Register(r_type_split_1_rs), .CLOCK(multiplexer_10_out));
  PC pc_1 (
    .Input(i_type_split_1_immediate), .Output(pc_1_output), .Plus_1(multiplexer_4_out),
    .Write(control_1_write_pc), .CLOCK(multiplexer_10_out));
  Comparator #(.width(4)) comparator_2 (.a(OP), .b(4'b1110), .eq(comparator_2_eq));  // open: gt, lt
  ROM #(.dataWidth(16)) rom_1 (.addr(pc_1_output), .data(rom_1_data));  // open: sel
  Multiplexer #(.width(8)) multiplexer_5 (
    .in0(registerfiles_1_register_2_out), .in1(i_type_split_1_immediate), .out(multiplexer_5_out),
    .sel(control_1_r_type_or_i_type));  // open: en
  Multiplexer #(.width(8)) multiplexer_6 (
    .in1(registerfiles_1_register_1_out), .out({multiplexer_6_out_2, multiplexer_6_out}),
    .sel(comparator_2_eq));  // open: in0, en
  ALU alu_1 (
    .A(registerfiles_1_register_1_out), .B(multiplexer_5_out), .Operation(control_1_alu_op),
    .Result(alu_1_result));
  Multiplexer #(.width(8)) multiplexer_7 (
    .in0(alu_1_result), .in1(ram_1_data), .out(multiplexer_7_out), .sel(control_1_load_byte));  // open: en
  Multiplexer #(.width(8)) multiplexer_8 (
    .in0(registerfiles_1_register_1_out), .in1(registerfiles_1_register_2_out), .out(multiplexer_8_out),
    .sel(not_2_out));  // open: en
  not not_2 (not_2_out, control_1_save_byte);
  alpaca alpaca_1 (.A(control_1_load_byte), .B(comparator_4_eq), .Out(alpaca_1_out));
  Hex_Digit_Display hex_digit_display_1 (.value(multiplexer_6_out));  // open: dp
  Hex_Digit_Display hex_digit_display_2 (.value(multiplexer_6_out_2));  // open: dp
  Multiplexer #(.width(8)) multiplexer_9 (
    .in0(i_type_split_1_immediate), .in1(alu_1_result), .out(multiplexer_9_out), .sel(alpaca_1_out));  // open: en
  RAM #(.bus("separate")) ram_1 (
    .addr(multiplexer_9_out), .din(multiplexer_8_out), .data(ram_1_data), .str(control_1_input_ram),
    .clk(multiplexer_10_out), .ld(control_1_output_ram));  // open: sel, clr
  Clock #(.highDuration(3), .lowDuration(3)) clock_1 (.out(clock_1_out));
  Multiplexer multiplexer_10 (.in0(clock_1_out), .out(multiplexer_10_out), .sel(comparator_3_eq));  // open: in1, en
  Comparator #(.width(4)) comparator_3 (.a(OP), .b(4'b1111), .eq(comparator_3_eq));  // open: gt, lt
  Comparator #(.width(4)) comparator_4 (.a(r_type_split_1_opcode), .b(4'b1100), .eq(comparator_4_eq));  // open: gt, lt

  // Notes on the sheet:
  //   0000 ADD
  //   0001 SUB
  //   0010 SLT
  //   0011
  //   0100 ADDI
  //   0101 BEQ
  //   0110
  //   0111 XOR
  //   1000 SB
  //   1001 J
  //   1010
  //   1011
  //   1100 LB
  //   1101 RAND
  //   1110 DISP
  //   1111 HALT
  //   contents of rom_1 (hex, n*v repeats v):
  //   4001 d400 e400 7a80 4a0a 2c80 7a80 4a01 5e00 f000
endmodule

module ALU (
  input  [7:0] A,
  input  [7:0] B,
  input  [2:0] Operation,
  output [7:0] Result
);

  wire [0:0] comparator_1_eq, comparator_1_gt, comparator_1_lt;
  wire [7:0] adder_1_out, adder_2_out, negator_1_out, randomnumbergenerator_1_out_3, xor_1_out;

  Negator negator_1 (.in(B), .out(negator_1_out));
  Adder adder_1 (.a(A), .b(B), .out(adder_1_out));  // open: cin, cout
  Adder adder_2 (.a(A), .b(negator_1_out), .out(adder_2_out));  // open: cin, cout
  Comparator comparator_1 (.a(A), .b(B), .gt(comparator_1_gt[0]), .eq(comparator_1_eq[0]), .lt(comparator_1_lt[0]));
  randomNumberGenerator randomnumbergenerator_1 (.Max(A), .out_3(randomnumbergenerator_1_out_3));  // open: CLOCK
  assign xor_1_out = A ^ B;  // XOR_Gate xor_1, 8 bits wide
  Multiplexer #(.select(3), .width(8)) multiplexer_1 (
    .in0(adder_1_out), .in1(adder_2_out), .in2({{7{1'b0}}, comparator_1_lt[0]}),
    .in3({{7{1'b0}}, comparator_1_eq[0]}), .in4({{7{1'b0}}, comparator_1_gt[0]}),
    .in5(randomnumbergenerator_1_out_3), .in6(xor_1_out), .out(Result), .sel(Operation));  // open: in7, en
endmodule

module registerFiles (
  input  [7:0] Write_Data,
  input  toWrite,
  input  [1:0] Write_Register,
  input  [1:0] Read_Register_1,
  input  toRead,
  input  [1:0] Read_Register_2,
  input  CLOCK,
  output [7:0] Register_1_OUT,
  output [7:0] Register_2_OUT
);

  wire decoder_1_out0, decoder_1_out1, decoder_1_out2, decoder_1_out3;
  wire [7:0] multiplexer_1_out, multiplexer_2_out, Register_1_q, Register_2_q, Register_3_q, Register_4_q;

  Decoder #(.select(2), .disabled(0)) decoder_1 (
    .out0(decoder_1_out0), .out1(decoder_1_out1), .out2(decoder_1_out2), .out3(decoder_1_out3),
    .sel(Write_Register), .en(toWrite));
  Register #(.trigger("falling")) Register_1 (
    .D(Write_Data), .en(decoder_1_out0), .Q(Register_1_q), .clk(CLOCK));  // open: clr
  Register #(.trigger("falling")) Register_2 (
    .D(Write_Data), .en(decoder_1_out1), .Q(Register_2_q), .clk(CLOCK));  // open: clr
  Register #(.trigger("falling")) Register_3 (
    .D(Write_Data), .en(decoder_1_out2), .Q(Register_3_q), .clk(CLOCK));  // open: clr
  Register #(.trigger("falling")) Register_4 (
    .D(Write_Data), .en(decoder_1_out3), .Q(Register_4_q), .clk(CLOCK));  // open: clr
  Multiplexer #(.select(2), .width(8)) multiplexer_1 (
    .in0(Register_1_q), .in1(Register_2_q), .in2(Register_3_q), .in3(Register_4_q), .out(multiplexer_1_out),
    .sel(Read_Register_2));  // open: en
  Multiplexer #(.select(2), .width(8)) multiplexer_2 (
    .in0(Register_1_q), .in1(Register_2_q), .in2(Register_3_q), .in3(Register_4_q), .out(multiplexer_2_out),
    .sel(Read_Register_1));  // open: en
  Multiplexer #(.width(8)) multiplexer_3 (
    .in0({8{1'b0}}), .in1(multiplexer_2_out), .out(Register_1_OUT), .sel(toRead));  // open: en
  Multiplexer #(.width(8)) multiplexer_4 (
    .in0({8{1'b0}}), .in1(multiplexer_1_out), .out(Register_2_OUT), .sel(toRead));  // open: en
endmodule

module randomNumberGenerator (
  input  [7:0] Max,
  input  CLOCK,
  output [7:0] out_3
);

  wire [7:0] divider_1_rem, multiplexer_1_out, negator_1_out, random_1_out;

  Random random_1 (.clk(CLOCK), .out(random_1_out));  // open: next, clr
  Multiplexer #(.width(8)) multiplexer_1 (
    .in0(random_1_out), .in1(negator_1_out), .out(multiplexer_1_out), .sel(random_1_out[7]));  // open: en
  Negator negator_1 (.in(random_1_out), .out(negator_1_out));
  Divider divider_1 (.a(multiplexer_1_out), .b(Max), .rem(divider_1_rem));  // open: out, upper
  Adder adder_1 (.a(divider_1_rem), .b(8'h1), .out(out_3));  // open: cin, cout
endmodule

module r_type_split (
  input  [15:0] Input,
  output [1:0] RD,
  output [1:0] RT,
  output [1:0] RS,
  output [3:0] Opcode
);


  assign Opcode = Input[15:12];
  assign RD = Input[7:6];
  assign RS = Input[11:10];
  assign RT = Input[9:8];
endmodule

module i_type_split (
  input  [15:0] Input,
  output [7:0] Immediate,
  output [1:0] RT,
  output [1:0] RS,
  output [3:0] Opcode
);


  assign Immediate = Input[7:0];
  assign Opcode = Input[15:12];
  assign RS = Input[11:10];
  assign RT = Input[9:8];
endmodule

module PC (
  input  [7:0] Input,
  input  Write,
  input  Plus_1,
  input  CLOCK,
  output [7:0] Output
);

  wire [7:0] adder_1_out, multiplexer_1_out;

  Multiplexer #(.width(8)) multiplexer_1 (
    .in0(Input), .in1(adder_1_out), .out(multiplexer_1_out), .sel(Plus_1));  // open: en
  Adder adder_1 (.a(8'h1), .b(Output), .out(adder_1_out));  // open: cin, cout
  Register #(.trigger("falling")) register_1 (.D(multiplexer_1_out), .en(Write), .Q(Output), .clk(CLOCK));  // open: clr
endmodule

module Control (
  input  [3:0] OP_CODE,
  output Save_Byte,
  output Read_RF,
  output Write_RF,
  output PC___1,
  output Write_PC,
  output Load_Byte,
  output R_Type_or_I_Type,
  output Input_RAM,
  output Output_RAM,
  output [2:0] ALU_OP
);

  wire [15:12] multiplexer_1_out;

  Multiplexer #(.select(4), .width(16)) multiplexer_1 (
    .in0(16'h1e), .in1(16'h21e), .in2(16'h41e), .in4(16'h5e), .in5(16'h61f), .in7(16'hc1e), .in8(16'hdb),
    .in9(16'h10), .in12(16'h13e), .in13(16'ha1e), .in14(16'h1b), .in15({16{1'b0}}),
    .out({multiplexer_1_out, ALU_OP, Output_RAM, Input_RAM, R_Type_or_I_Type, Load_Byte, Write_PC, PC___1, Write_RF, Read_RF, Save_Byte}),
    .sel(OP_CODE));  // open: in3, in6, in10, in11, en

  // Notes on the sheet:
  //   SB
  //   0000 ADD
  //   0001 SUB
  //   0010 SLT
  //   0011
  //   0100 ADDI
  //   0101 BEQ
  //   0110
  //   0111 XOR
  //   1000 SB
  //   1001 J
  //   1010
  //   1011
  //   1100 LB
  //   1101 RAND
  //   1110 DISP
  //   1111 HALT
  //   SUB
  //   SLT
  //   BEQ
  //   XOR
  //   rand
  //   lb
  //   halt
  //   ADD
  //   ADDI
  //   J
  //   disp
endmodule

module alpaca (
  input  A,
  input  B,
  output Out
);

  wire not_1_out;

  not not_1 (not_1_out, A);
  and and_1 (Out, not_1_out, B);
endmodule
